// Logisim project CPU32.circ as structural Verilog: 1 circuit, main circuit main
module main (
);

  wire C1, clock_2_out, R0_WE, R1_WE, R2_WE, R3_WE, R4_WE, R5_WE, R6_WE, R7_WE, R8_WE, R9_WE, R10_WE, R11_WE,
       R12_WE, R13_WE, R14_WE, R15_WE;
  wire [31:0] adder_1_out, adder_2_out, ALU_OUT, and_1_out, INSTRUCTION_ROM_data, MUX_A_OUT, MUX_B_OUT,
       or_1_out, PC_q, R, R0_OUT, R1_OUT, R2_OUT, R3, R3_OUT, R4_OUT, R5, R5_OUT, R6, R6_OUT, R7, R7_OUT,
       R8_OUT, R9, R9_OUT, R10, R10_OUT, R11, R11_OUT, R12, R12_OUT, R13, R13_OUT, R14, R14_OUT, R15,
       R15_OUT, RAM_OUT, subtractor_1_out, xor_1_out;

  Clock clock_1 (.out(C1));
  Register #(.width(32)) R0 (.D(32'h9), .clk(C1), .Q(R0_OUT), .clr(1'b0));  // open: en
  Register #(.width(32)) R2 (.D(32'h5), .en(R2_WE), .clk(C1), .Q(R2_OUT), .clr(1'b0));
  Register #(.width(32)) R4 (.D(32'h1), .en(1'b1), .clk(C1), .Q(R4_OUT), .clr(1'b0));
  Register #(.width(32)) u_R6 (.D(R6), .en(R6_WE), .clk(C1), .Q(R6_OUT), .clr(1'b0));
  Register #(.width(32)) R8 (.D(R), .en(R8_WE), .clk(C1), .Q(R8_OUT), .clr(1'b0));
  Register #(.width(32)) u_R10 (.D(R10), .en(R10_WE), .clk(C1), .Q(R10_OUT), .clr(1'b0));
  Register #(.width(32)) u_R14 (.D(R14), .en(R14_WE), .clk(C1), .Q(R14_OUT), .clr(1'b0));
  Register #(.width(32)) u_R12 (.D(R12), .en(R12_WE), .clk(C1), .Q(R12_OUT), .clr(1'b0));
  Register #(.width(32)) R1 (.D(32'h7), .en(1'b1), .clk(C1), .Q(R1_OUT), .clr(1'b0));
  Register #(.width(32)) u_R3 (.D(R3), .en(R3_WE), .clk(C1), .Q(R3_OUT), .clr(1'b0));
  Register #(.width(32)) u_R5 (.D(R5), .en(R5_WE), .clk(C1), .Q(R5_OUT), .clr(1'b0));
  Register #(.width(32)) u_R7 (.D(R7), .en(R7_WE), .clk(C1), .Q(R7_OUT), .clr(1'b0));
  Register #(.width(32)) u_R9 (.D(R9), .en(R9_WE), .clk(C1), .Q(R9_OUT), .clr(1'b0));
  Register #(.width(32)) u_R11 (.D(R11), .en(R11_WE), .clk(C1), .Q(R11_OUT), .clr(1'b0));
  Register #(.width(32)) u_R13 (.D(R13), .en(R13_WE), .clk(C1), .Q(R13_OUT), .clr(1'b0));
  Register #(.width(32)) u_R15 (.D(R15), .en(R15_WE), .clk(C1), .Q(R15_OUT), .clr(1'b0));
  Register #(.width(32)) PC (.D(adder_1_out), .en(1'b1), .clk(C1), .Q(PC_q), .clr(1'b0));
  Decoder #(.select(4)) decoder_1 (
    .out0(R0_WE), .out1(R1_WE), .out2(R2_WE), .out3(R3_WE), .out4(R4_WE), .out5(R5_WE), .out6(R6_WE),
    .out7(R7_WE), .out8(R8_WE), .out9(R9_WE), .out10(R10_WE), .out11(R11_WE), .out12(R12_WE), .out13(R13_WE),
    .out14(R14_WE), .out15(R15_WE), .sel(4'b0010), .en(1'b1));
  Multiplexer #(.select(4), .width(32)) multiplexer_1 (
    .in0(R0_OUT), .in1(R1_OUT), .in2(R2_OUT), .in3(R3_OUT), .in4(R4_OUT), .in5(R5_OUT), .in6(R6_OUT),
    .in7(R7_OUT), .in8(R8_OUT), .in9(R9_OUT), .in10(R10_OUT), .in11(R11_OUT), .in12(R12_OUT), .in13(R13_OUT),
    .in14(R14_OUT), .in15(R15_OUT), .out(MUX_B_OUT), .sel(4'b0000));
  Multiplexer #(.select(4), .width(32)) multiplexer_2 (
    .in0(R0_OUT), .in1(R1_OUT), .in2(R2_OUT), .in3(R3_OUT), .in4(R4_OUT), .in5(R5_OUT), .in6(R6_OUT),
    .in7(R7_OUT), .in8(R8_OUT), .in9(R9_OUT), .in10(R10_OUT), .in11(R11_OUT), .in12(R12_OUT), .in13(R13_OUT),
    .in14(R14_OUT), .in15(R15_OUT), .out(MUX_A_OUT), .sel(4'b0000));
  Adder #(.width(32)) adder_1 (.a(PC_q), .b(32'h1), .out(adder_1_out), .cin(1'b0));  // open: cout
  ROM #(.dataWidth(32)) INSTRUCTION_ROM (.addr(PC_q[7:0]), .data(INSTRUCTION_ROM_data));
  Adder #(.width(32)) adder_2 (.a(MUX_A_OUT), .b(MUX_B_OUT), .out(adder_2_out), .cin(1'b0));  // open: cout
  RAM #(.addrWidth(12), .dataWidth(32)) DATA_RAM (
    .addr(MUX_A_OUT[11:0]), .we(1'b1), .oe(1'b1), .clk(clock_2_out), .din(MUX_B_OUT), .dout(RAM_OUT));
  Clock clock_2 (.out(clock_2_out));
  Subtractor #(.width(32)) subtractor_1 (.a(MUX_A_OUT), .b(MUX_B_OUT), .out(subtractor_1_out));  // open: bin, bout
  assign and_1_out = MUX_A_OUT & MUX_B_OUT;  // AND_Gate and_1, 32 bits wide
  assign or_1_out = MUX_A_OUT | MUX_B_OUT;  // OR_Gate or_1, 32 bits wide
  assign xor_1_out = MUX_A_OUT ^ MUX_B_OUT;  // XOR_Gate xor_1, 32 bits wide
  Multiplexer #(.select(3), .width(32)) multiplexer_3 (
    .in0(adder_2_out), .in1(subtractor_1_out), .in2(and_1_out), .in5(or_1_out), .in7(xor_1_out),
    .out(ALU_OUT), .sel(3'b010));  // open: in3, in4, in6
  Multiplexer #(.select(2), .width(32)) multiplexer_4 (
    .in0(RAM_OUT), .in1(ALU_OUT), .in2({32{1'b0}}), .in3(32'h1), .out(R), .sel(2'b00));
  Hex_Digit_Display hex_digit_display_1 (.value(R[31:28]));  // open: dp
  Hex_Digit_Display hex_digit_display_2 (.value(R[15:12]));  // open: dp
  Hex_Digit_Display hex_digit_display_3 (.value(R[27:24]));  // open: dp
  Hex_Digit_Display hex_digit_display_4 (.value(R[11:8]));  // open: dp
  Hex_Digit_Display hex_digit_display_5 (.value(R[23:20]));  // open: dp
  Hex_Digit_Display hex_digit_display_6 (.value(R[19:16]));  // open: dp
  Hex_Digit_Display hex_digit_display_7 (.value(R[7:4]));  // open: dp
  Hex_Digit_Display hex_digit_display_8 (.value(R[3:0]));  // open: dp
endmodule
